// Logisim project regfile.circ as structural Verilog: 1 circuit, main circuit RegFile
module RegFile (
  input  [4:0] RD,
  input  [4:0] RS1,
  input  [4:0] RS2,
  input  [31:0] W,
  input  WE,
  input  Clk,
  output [31:0] s0,
  output [31:0] s1,
  output [31:0] t0,
  output [31:0] t1,
  output [31:0] a0,
  output [31:0] ra,
  output [31:0] sp,
  output [31:0] R1,
  output [31:0] R2
);

  wire demultiplexer_1_out0, demultiplexer_1_out1, demultiplexer_1_out2, demultiplexer_1_out5,
       demultiplexer_1_out6, demultiplexer_1_out8, demultiplexer_1_out9, demultiplexer_1_out10,
       demultiplexer_1_out11;
  wire [31:0] a1, register_1_q;

  Demultiplexer #(.select(5)) demultiplexer_1 (
    .out0(demultiplexer_1_out0), .out1(demultiplexer_1_out1), .out2(demultiplexer_1_out2),
    .out5(demultiplexer_1_out5), .out6(demultiplexer_1_out6), .out8(demultiplexer_1_out8),
    .out9(demultiplexer_1_out9), .out10(demultiplexer_1_out10), .out11(demultiplexer_1_out11), .in(WE),
    .sel(RD));  // open: out3, out4, out7, out12, out13, out14, out15, out16, out17, out18, out19, out20, out21, out22, out23, out24, out25, out26, out27, out28, out29, out30, out31, en
  Register #(.width(32)) register_1 (
    .D({32{1'b0}}), .en(demultiplexer_1_out0), .Q(register_1_q), .clk(Clk));  // open: clr
  Register #(.width(32)) register_2 (.D(W), .en(demultiplexer_1_out1), .Q(ra), .clk(Clk));  // open: clr
  Register #(.width(32)) register_3 (.D(W), .en(demultiplexer_1_out2), .Q(sp), .clk(Clk));  // open: clr
  Register #(.width(32)) register_4 (.D(W), .en(demultiplexer_1_out5), .Q(t0), .clk(Clk));  // open: clr
  Register #(.width(32)) register_5 (.D(W), .en(demultiplexer_1_out6), .Q(t1), .clk(Clk));  // open: clr
  Register #(.width(32)) register_6 (.D(W), .en(demultiplexer_1_out8), .Q(s0), .clk(Clk));  // open: clr
  Register #(.width(32)) register_7 (.D(W), .en(demultiplexer_1_out9), .Q(s1), .clk(Clk));  // open: clr
  Register #(.width(32)) register_8 (.D(W), .en(demultiplexer_1_out10), .Q(a0), .clk(Clk));  // open: clr
  Register #(.width(32)) register_9 (.D(W), .en(demultiplexer_1_out11), .Q(a1), .clk(Clk));  // open: clr
  Multiplexer #(.select(5), .width(32)) multiplexer_1 (
    .in0({32{1'b0}}), .in1(ra), .in2(sp), .in5(t0), .in6(t1), .in8(s0), .in9(s1), .in10(a0), .in11(a1),
    .out(R1), .sel(RS1));  // open: in3, in4, in7, in12, in13, in14, in15, in16, in17, in18, in19, in20, in21, in22, in23, in24, in25, in26, in27, in28, in29, in30, in31, en
  Multiplexer #(.select(5), .width(32)) multiplexer_2 (
    .in0({32{1'b0}}), .in1(ra), .in2(sp), .in5(t0), .in6(t1), .in8(s0), .in9(s1), .in10(a0), .in11(a1),
    .out(R2), .sel(RS2));  // open: in3, in4, in7, in12, in13, in14, in15, in16, in17, in18, in19, in20, in21, in22, in23, in24, in25, in26, in27, in28, in29, in30, in31, en
  // also tied to GND on the sheet: {register_1_q[0], register_1_q[1], register_1_q[2], register_1_q[3], register_1_q[4], register_1_q[5], register_1_q[6], register_1_q[7], register_1_q[8], register_1_q[9], register_1_q[10], register_1_q[11], register_1_q[12], register_1_q[13], register_1_q[14], register_1_q[15], register_1_q[16], register_1_q[17], register_1_q[18], register_1_q[19], register_1_q[20], register_1_q[21], register_1_q[22], register_1_q[23], register_1_q[24], register_1_q[25], register_1_q[26], register_1_q[27], register_1_q[28], register_1_q[29], register_1_q[30], register_1_q[31]}

  // Notes on the sheet:
  //   Write Register
  //   Read Register 1
  //   Read Register 2
  //   Write Data
  //   Write Enable
  //   Clock
  //   NOTE
  //   Please do not modify/replace/move/change/delete/etc input and output pins
  //   These are debug/test outputs from your circuit
  //   Read Data 1
  //   Read Data 2
endmodule
